// Logisim project лаба1 ок.circ as structural Verilog
module \начало  (
  input  in_1,
  input  in_2,
  input  in_3,
  input  in_4,
  output out_5,
  output out_6,
  output out_7
);
endmodule

module \удача  (
  input  a,
  input  b,
  input  c,
  input  d,
  output x,
  output y,
  output z
);

  wire and_1_out, and_2_out, and_3_out, and_4_out, not_1_out, not_2_out, not_3_out, not_4_out, not_5_out;

  not not_1 (not_1_out, a);
  and and_1 (and_1_out, not_1_out, c);
  not not_2 (not_2_out, a);
  and and_2 (and_2_out, not_2_out, b);
  not not_3 (not_3_out, a);
  and and_3 (and_3_out, not_3_out, not_4_out, d);
  not not_4 (not_4_out, c);
  not not_5 (not_5_out, a);
  and and_4 (and_4_out, not_5_out, b);
  or or_1 (y, and_1_out, and_2_out);
  or or_2 (z, and_3_out, and_4_out);

  assign x = a;
endmodule
