// Logisim project лаба2 ок.circ as structural Verilog: 5 circuits, main circuit Вентиль "НЕ"
module \Вентиль__НЕ  (
  input  in_1
);

  wire transistor_1_out;

  Transistor transistor_1 (.in(1'b1), .out(transistor_1_out), .gate(in_1));
  Transistor #(.\type ("n")) transistor_2 (.in(1'b0), .out(transistor_1_out), .gate(in_1));
  // Probe on transistor_1_out
endmodule

module \Вентиль__И  (
  input  in_1,
  input  in_2
);

  wire transistor_1_out, transistor_2_out;

  Transistor transistor_1 (.in(1'b0), .out(transistor_1_out), .gate(in_2));
  Transistor #(.\type ("n")) transistor_2 (.in(1'b1), .out(transistor_2_out), .gate(in_1));
  Transistor #(.\type ("n")) transistor_3 (.in(transistor_2_out), .out(transistor_1_out), .gate(in_2));
  Transistor transistor_4 (.in(1'b0), .out(transistor_1_out), .gate(in_1));
  // Probe on transistor_1_out
endmodule

module \Вентиль__ИЛИ  (
  input  in_1,
  input  in_2
);

  wire transistor_1_out, transistor_4_out;

  Transistor #(.\type ("n")) transistor_1 (.in(1'b1), .out(transistor_1_out), .gate(in_1));
  Transistor #(.\type ("n")) transistor_2 (.in(1'b1), .out(transistor_1_out), .gate(in_2));
  // Probe on transistor_1_out
  Transistor transistor_3 (.in(transistor_4_out), .out(transistor_1_out), .gate(in_2));
  Transistor transistor_4 (.in(1'b0), .out(transistor_4_out), .gate(in_1));
endmodule

module \Вентиль__И_НЕ  (
  input  in_1,
  input  in_2
);

  wire transistor_1_out, transistor_4_out;

  Transistor transistor_1 (.in(1'b1), .out(transistor_1_out), .gate(in_1));
  Transistor transistor_2 (.in(1'b1), .out(transistor_1_out), .gate(in_2));
  Transistor #(.\type ("n")) transistor_3 (.in(transistor_4_out), .out(transistor_1_out), .gate(in_2));
  Transistor #(.\type ("n")) transistor_4 (.in(1'b0), .out(transistor_4_out), .gate(in_1));
  // Probe on transistor_1_out
endmodule

module \Вентиль__ИЛИ_НЕ  (
  input  in_1,
  input  in_2
);

  wire transistor_1_out, transistor_2_out;

  Transistor #(.\type ("n")) transistor_1 (.in(1'b0), .out(transistor_1_out), .gate(in_2));
  Transistor transistor_2 (.in(1'b1), .out(transistor_2_out), .gate(in_1));
  Transistor transistor_3 (.in(transistor_2_out), .out(transistor_1_out), .gate(in_2));
  Transistor #(.\type ("n")) transistor_4 (.in(1'b0), .out(transistor_1_out), .gate(in_1));
  // Probe on transistor_1_out
endmodule
